# Fritzing sketch HumanDitection1 (saved by Fritzing 0.9.5d)
breadboards: 1

parts:
  Part1 = Arduino Uno (Rev3)
  Part2 = HC-SR501 Body Sensor Module

nets:
  N1: Part1.D2, Part2.OUT
  5V: Part1.5V, Part2.VCC
  GND: Part1.GND, Part2.GND

custom parts:
  HC-SR501 Body Sensor Module: Pyroelectric Infrared PIR Motion Sensor Detector Module
