# Fritzing sketch HumanDitection2 (saved by Fritzing 0.9.5d)
breadboards: 1

parts:
  Part1 = Arduino Uno (Rev3)
  Part2 = HC-SR501 Body Sensor Module
  LED1 = smd LED [color="White (4500K)" package="0805 [SMD]"]

nets:
  N1: Part1.D11_PWM/MOSI, LED1.anode
  N2: Part1.D2, Part2.OUT
  5V: Part1.5V, Part2.VCC
  GND: Part1.GND, Part2.GND, LED1.cathode

custom parts:
  HC-SR501 Body Sensor Module: Pyroelectric Infrared PIR Motion Sensor Detector Module
